// Logisim project CPU.circ as structural Verilog: 16 circuits, main circuit main
module main (
  output [9:0] out_1,
  output [9:0] out_2,
  output [9:0] out_3,
  output [9:0] out_4,
  output [9:0] out_5,
  output [9:0] out_6,
  output [9:0] out_7,
  output ignore,
  output halt
);

  wire and_3_out, CLK, clock_1_out, comparator_1_lt, comparator_2_lt, control_unit_1_bnez,
       control_unit_1_halt, control_unit_1_nop, control_unit_1_subtract, Decoder_Enable, JMP, not_2_out,
       not_3_out, not_4_out, or_1_out, t_ff_1_q, TClock;
  wire [0:0] noHLT;
  wire [1:0] counter_2_q, Upper_2_bits;
  wire [2:0] B, control_unit_1_alusel, rom_1_data;
  wire [3:0] B_Sel;
  wire [4:0] counter_1_q, multiplexer_2_out, pc_1_out, pcadder_1_out;
  wire [6:0] adder_1_out, adder_2_out, ASCII, decoder_1_out0, LSB, MiddleBits;
  wire [7:0] multiplexer_5_out;
  wire [9:0] Data, mainalu_1_output, multiplexer_1_out, multiplexer_3_out, multiplexer_4_out;
  wire [23:13] ram_1_data;

  PCAdder pcadder_1 (._1_or_5(multiplexer_2_out), .IN(pc_1_out), .OUT(pcadder_1_out));  // open: COUT
  PC pc_1 (.CLK(CLK), .OUT(pc_1_out), .IN(pcadder_1_out));
  RAM #(.addrWidth(5), .dataWidth(24), .bus("separate")) ram_1 (
    .addr(pc_1_out), .data({ram_1_data, B, Data}));  // open: din, str, sel, clk, ld, clr
  not not_1 (noHLT[0], control_unit_1_halt);
  Multiplexer #(.select(3), .width(10)) multiplexer_1 (
    .in0(out_1), .in1(out_2), .in2(out_3), .in3(out_4), .in4(out_5), .in5(out_6), .in6(out_7),
    .out(multiplexer_1_out), .sel(ram_1_data[18:16]));  // open: in7, en
  Multiplexer #(.width(5)) multiplexer_2 (
    .in0({4'b0000, noHLT[0]}), .in1(Data[4:0]), .out(multiplexer_2_out), .sel(JMP));  // open: en
  Decoder #(.select(3)) decoder_1 (
    .out0(decoder_1_out0[0]), .out1(decoder_1_out0[1]), .out2(decoder_1_out0[2]), .out3(decoder_1_out0[3]),
    .out4(decoder_1_out0[4]), .out5(decoder_1_out0[5]), .out6(decoder_1_out0[6]), .sel(ram_1_data[18:16]),
    .en(Decoder_Enable));  // open: out7
  Control_Unit control_unit_1 (
    .opcode(ram_1_data[23:19]), .B(B), .BSel(B_Sel), .ALUSel(control_unit_1_alusel),
    .Subtract(control_unit_1_subtract), .BNEZ(control_unit_1_bnez), .NOP(control_unit_1_nop),
    .HALT(control_unit_1_halt));
  or or_1 (or_1_out, multiplexer_1_out[0], multiplexer_1_out[1], multiplexer_1_out[2], multiplexer_1_out[3], multiplexer_1_out[4], multiplexer_1_out[5], multiplexer_1_out[6], multiplexer_1_out[7], multiplexer_1_out[8], multiplexer_1_out[9]);
  Multiplexer #(.select(3), .width(10)) multiplexer_3 (
    .in0(out_1), .in1(out_2), .in2(out_3), .in3(out_4), .in4(out_5), .in5(out_6), .in6(out_7),
    .out(multiplexer_3_out), .sel(ram_1_data[15:13]));  // open: in7, en
  and and_1 (JMP, control_unit_1_bnez, or_1_out);
  MainALU mainalu_1 (
    .CIN(control_unit_1_subtract), .A(multiplexer_3_out), .Output(mainalu_1_output),
    .ALU_Control(control_unit_1_alusel), .B(multiplexer_4_out));
  not not_2 (not_2_out, control_unit_1_bnez);
  and and_2 (Decoder_Enable, not_2_out, not_3_out);
  not not_3 (not_3_out, control_unit_1_nop);
  Multiplexer #(.select(4), .width(10)) multiplexer_4 (
    .in0(out_1), .in1(out_2), .in2(out_3), .in3(out_4), .in4(out_5), .in5(out_6), .in6(out_7), .in7(Data),
    .in8({10{1'b0}}), .out(multiplexer_4_out), .sel(B_Sel));  // open: in9, in10, in11, in12, in13, in14, in15, en
  Register_Bank register_bank_1 (
    .Decoder_Input(decoder_1_out0), .Data(mainalu_1_output), .Clock(CLK), .Out0(out_1), .Out1(out_2),
    .Out2(out_3), .Out3(out_4), .Out4(out_5), .Out5(out_6), .Out6(out_7));
  TTY #(.rows(33), .cols(4)) tty_1 (.data(ASCII), .clk(TClock));  // open: we, clr
  // Probe on out_1
  // Probe on out_5
  Counter #(.width(5), .max('h1f), .ongoal("stay")) counter_1 (
    .Q(counter_1_q), .carry(halt), .clk(CLK));  // open: load, D, count, clr
  // Probe on out_2
  // Probe on out_6
  Multiplexer #(.select(3), .width(10)) multiplexer_5 (
    .in0(out_1), .in1(out_2), .in2(out_3), .in3(out_4), .in4(out_5), .in5(out_6), .in6(out_7),
    .out({Upper_2_bits, multiplexer_5_out}), .sel(rom_1_data));  // open: in7, en
  not not_4 (not_4_out, halt);
  Clock clock_1 (.out(clock_1_out));
  ROM #(.addrWidth(5), .dataWidth(3)) rom_1 (.addr(counter_1_q), .data(rom_1_data));  // open: sel
  and and_3 (and_3_out, not_4_out, clock_1_out);
  not not_5 (TClock, and_3_out);
  // Probe on out_3
  // Probe on out_7
  // Probe on out_4
  Comparator #(.width(7)) comparator_1 (
    .a(7'b0111001), .b({3'b011, multiplexer_5_out[3:0]}), .lt(comparator_1_lt));  // open: gt, eq
  Comparator #(.width(7)) comparator_2 (
    .a(7'b0111001), .b({3'b011, multiplexer_5_out[7:4]}), .lt(comparator_2_lt));  // open: gt, eq
  T_Flip_Flop t_ff_1 (.clk(and_3_out), .T(1'b1), .Q(t_ff_1_q));  // open: Qn, preset, reset, en
  T_Flip_Flop t_ff_2 (.clk(t_ff_1_q), .T(1'b1), .Q(CLK));  // open: Qn, preset, reset, en
  Adder #(.width(7)) adder_1 (
    .a({3'b011, multiplexer_5_out[3:0]}), .b(7'b0000111), .out(adder_1_out));  // open: cin, cout
  Adder #(.width(7)) adder_2 (
    .a({3'b011, multiplexer_5_out[7:4]}), .b(7'b0000111), .out(adder_2_out));  // open: cin, cout
  Multiplexer #(.select(2), .width(7)) multiplexer_6 (
    .in0({5'b01100, Upper_2_bits}), .in1(MiddleBits), .in2(LSB), .in3(7'b0100000), .out(ASCII),
    .sel(counter_2_q));  // open: en
  Counter #(.width(2), .max('h3)) counter_2 (.Q(counter_2_q), .clk(TClock));  // open: load, D, count, carry, clr
  Multiplexer #(.width(7), .disabled(0), .enable("false")) multiplexer_7 (
    .in0({3'b011, multiplexer_5_out[3:0]}), .in1(adder_1_out), .out(LSB), .sel(comparator_1_lt));
  Multiplexer #(.width(7), .disabled(0), .enable("false")) multiplexer_8 (
    .in0({3'b011, multiplexer_5_out[7:4]}), .in1(adder_2_out), .out(MiddleBits), .sel(comparator_2_lt));
  T_Flip_Flop t_ff_3 (.clk(CLK), .T(1'b1), .Q(ignore));  // open: Qn, preset, reset, en

  // Other names for the same wires on the sheet: R0[9:0] = out_1; R1[9:0] = out_2; R2[9:0] = out_3; R3[9:0] = out_4;
  //   R4[9:0] = out_5; R5[9:0] = out_6; R6[9:0] = out_7

  // Notes on the sheet:
  //   HANDLES BNEZ AND NOP
  //   DO NOT PUT ANY PINS ON THE main circuit.  (You should not need any anyway.)
  //   0F5
  //   0F5
  //   25A
  //   050
  //   2FF
  //   30A
  //   34F
  //   0F5
  //   1EA
  //   07A
  //   29B
  //   165
  //   10F
  //   0F5
  //   0AA
  //   0AA
  //   05A
  //   00A
  //   0FA
  //   104
  //   0B4
  //   165
  //   165
  //   001
  //   001
  //   000
  //   000
  //   000
  //   000
  //   000
  //   ???
  //   There is no Reset.  Just Ctrl-r, then load test.txt into your RAM, and then Ctrl-k
  //   You must  use the CLK tunnel for the source of your clock.  R0-R6 are the other tunnels you need to connect
  //   contents of rom_1 (hex, n*v repeats v):
  //   0 0 0 1 2 3 4 5 6 2 3 4 5 6 0 0 0 1 3 4 6 3 5 5 8*6
endmodule

module Register (
  input  in_1,
  input  [9:0] in_2,
  output [9:0] out_3
);

  D_Flip_Flop d_ff_1 (.clk(in_1), .D(in_2[0]), .Q(out_3[0]));  // open: Qn, preset, en, reset
  D_Flip_Flop d_ff_2 (.clk(in_1), .D(in_2[1]), .Q(out_3[1]));  // open: Qn, preset, en, reset
  D_Flip_Flop d_ff_3 (.clk(in_1), .D(in_2[2]), .Q(out_3[2]));  // open: Qn, preset, en, reset
  D_Flip_Flop d_ff_4 (.clk(in_1), .D(in_2[3]), .Q(out_3[3]));  // open: Qn, preset, en, reset
  D_Flip_Flop d_ff_5 (.clk(in_1), .D(in_2[4]), .Q(out_3[4]));  // open: Qn, preset, en, reset
  D_Flip_Flop d_ff_6 (.clk(in_1), .D(in_2[5]), .Q(out_3[5]));  // open: Qn, preset, en, reset
  D_Flip_Flop d_ff_7 (.clk(in_1), .D(in_2[6]), .Q(out_3[6]));  // open: Qn, preset, en, reset
  D_Flip_Flop d_ff_8 (.clk(in_1), .D(in_2[7]), .Q(out_3[7]));  // open: Qn, preset, en, reset
  D_Flip_Flop d_ff_9 (.clk(in_1), .D(in_2[8]), .Q(out_3[8]));  // open: Qn, preset, en, reset
  D_Flip_Flop d_ff_10 (.clk(in_1), .D(in_2[9]), .Q(out_3[9]));  // open: Qn, preset, en, reset
endmodule

module Register_Bank (
  input  [6:0] Decoder_Input,
  input  Clock,
  input  [9:0] Data,
  output [9:0] Out0,
  output [9:0] Out1,
  output [9:0] Out2,
  output [9:0] Out3,
  output [9:0] Out4,
  output [9:0] Out5,
  output [9:0] Out6
);

  wire and_1_out, and_2_out, and_3_out, and_4_out, and_5_out, and_6_out, and_7_out;

  Register _0 (.in_1(and_1_out), .in_2(Data), .out_3(Out0));
  Register _1 (.in_1(and_2_out), .in_2(Data), .out_3(Out1));
  Register _3 (.in_1(and_3_out), .in_2(Data), .out_3(Out2));
  Register _4 (.in_1(and_4_out), .in_2(Data), .out_3(Out3));
  Register _5 (.in_1(and_5_out), .in_2(Data), .out_3(Out4));
  Register register_1 (.in_1(and_6_out), .in_2(Data), .out_3(Out5));
  Register register_2 (.in_1(and_7_out), .in_2(Data), .out_3(Out6));
  and and_1 (and_1_out, Decoder_Input[0], Clock);
  and and_2 (and_2_out, Decoder_Input[1], Clock);
  and and_3 (and_3_out, Decoder_Input[2], Clock);
  and and_4 (and_4_out, Decoder_Input[3], Clock);
  and and_5 (and_5_out, Decoder_Input[4], Clock);
  and and_6 (and_6_out, Decoder_Input[5], Clock);
  and and_7 (and_7_out, Decoder_Input[6], Clock);
endmodule

// CU
module Control_Unit (
  input  [4:0] opcode,
  input  [2:0] B,
  output [2:0] ALUSel,
  output Subtract,
  output NOP,
  output BNEZ,
  output [3:0] BSel,
  output HALT
);

  wire BNEZ_Check_out, NOP_Check_out, xor_1_out;

  Multiplexer #(.select(4)) multiplexer_1 (
    .in0(1'b0), .in1(1'b0), .in2(1'b0), .in3(1'b0), .in4(1'b0), .in5(1'b0), .in6(1'b0), .in7(1'b1),
    .in8(1'b0), .in9(1'b1), .in10(1'b0), .in11(1'b0), .in12(1'b0), .out(Subtract), .sel(opcode[3:0]));  // open: in13, in14, in15, en
  // Probe on Subtract
  Multiplexer #(.select(4), .width(3)) multiplexer_2 (
    .in0(3'b000), .in1(3'b001), .in2(3'b010), .in3(3'b011), .in4(3'b100), .in5(3'b101), .in6(3'b110),
    .in7(3'b011), .in8(3'b011), .in9(3'b011), .in10(3'b111), .in11(3'b000), .in12(3'b000), .out(ALUSel),
    .sel(opcode[3:0]));  // open: in13, in14, in15, en
  Multiplexer #(.select(4), .width(4)) multiplexer_3 (
    .in0(4'b0000), .in1(4'b0001), .in2(4'b0010), .in3(4'b0011), .in4(4'b0100), .in5(4'b0101), .in6(4'b0110),
    .in8(4'b0111), .out(BSel), .sel({opcode[3], B}));  // open: in7, in9, in10, in11, in12, in13, in14, in15, en
  // Probe on ALUSel
  // Probe on BSel
  and NOP_Check (NOP_Check_out, opcode[3], opcode[2]);
  and BNEZ_Check (BNEZ_Check_out, opcode[0], opcode[1], opcode[3]);
  xor xor_1 (xor_1_out, opcode[3], opcode[4]);
  xor xor_2 (NOP, NOP_Check_out, opcode[4]);
  and and_1 (BNEZ, BNEZ_Check_out, xor_1_out);

  assign HALT = opcode[4];

  // Other names for the same wires on the sheet: B2[3:0] = {opcode[3], B}
endmodule

// Main ALU
module MainALU (
  input  [9:0] A,
  input  [9:0] B,
  input  CIN,
  input  [2:0] ALU_Control,
  output [9:0] Output
);

  wire n5bitalu_2_c5;
  wire [0:0] pcadder_2_cout;
  wire [9:0] BNEW, not_1_out, pcadder_2_out;

  _5BitALU u_5bitalu_1 (
    .C4(Output[9]), .C3(Output[8]), .C2(Output[7]), .C1(Output[6]), .C0(Output[5]), .B4(BNEW[9]),
    .B3(BNEW[8]), .B2(BNEW[7]), .B1(BNEW[6]), .B0(BNEW[5]), .A4(A[9]), .A3(A[8]), .A2(A[7]), .A1(A[6]),
    .A0(A[5]), .CIN(n5bitalu_2_c5), .S2(ALU_Control[2]), .S1(ALU_Control[1]), .S0(ALU_Control[0]),
    .SRLBit(1'b0));  // open: C5
  _5BitALU u_5bitalu_2 (
    .C5(n5bitalu_2_c5), .C4(Output[4]), .C3(Output[3]), .C2(Output[2]), .C1(Output[1]), .C0(Output[0]),
    .B4(BNEW[4]), .B3(BNEW[3]), .B2(BNEW[2]), .B1(BNEW[1]), .B0(BNEW[0]), .A4(A[4]), .A3(A[3]), .A2(A[2]),
    .A1(A[1]), .A0(A[0]), .CIN(1'b0), .S2(ALU_Control[2]), .S1(ALU_Control[1]), .S0(ALU_Control[0]),
    .SRLBit(A[5]));
  PCAdder pcadder_1 (
    ._1_or_5({4'b0000, pcadder_2_cout[0]}), .IN(not_1_out[9:5]), .OUT(pcadder_2_out[9:5]));  // open: COUT
  assign not_1_out = ~B;  // NOT_Gate not_1, 10 bits wide
  // Probe on pcadder_2_out
  PCAdder pcadder_2 (._1_or_5(5'b00001), .COUT(pcadder_2_cout[0]), .IN(not_1_out[4:0]), .OUT(pcadder_2_out[4:0]));
  Multiplexer #(.width(10)) multiplexer_1 (.in0(B), .in1(pcadder_2_out), .out(BNEW), .sel(CIN));  // open: en
  // Probe on BNEW
endmodule

module PC (
  input  CLK,
  input  [4:0] IN,
  output [4:0] OUT
);

  D_Flip_Flop #(.trigger("falling")) d_ff_1 (.clk(CLK), .D(IN[4]), .Q(OUT[4]));  // open: Qn, preset, en, reset
  D_Flip_Flop #(.trigger("falling")) d_ff_2 (.clk(CLK), .D(IN[3]), .Q(OUT[3]));  // open: Qn, preset, en, reset
  D_Flip_Flop #(.trigger("falling")) d_ff_3 (.clk(CLK), .D(IN[2]), .Q(OUT[2]));  // open: Qn, preset, en, reset
  D_Flip_Flop #(.trigger("falling")) d_ff_4 (.clk(CLK), .D(IN[1]), .Q(OUT[1]));  // open: Qn, preset, en, reset
  D_Flip_Flop #(.trigger("falling")) d_ff_5 (.clk(CLK), .D(IN[0]), .Q(OUT[0]));  // open: Qn, preset, en, reset
endmodule

// 5bitALU
module _5BitALU (
  input  SRLBit,
  input  B4,
  input  B3,
  input  B2,
  input  B1,
  input  B0,
  input  A4,
  input  A3,
  input  A2,
  input  A1,
  input  A0,
  input  CIN,
  input  S2,
  input  S1,
  input  S0,
  output C5,
  output C4,
  output C3,
  output C2,
  output C1,
  output C0
);

  wire [4:0] ANDout, NOTout, ORout, SLRout;
  wire [5:0] ADDout, SLLout;

  // Probe on ADDout[5]
  ADD add_1 (
    .C5(ADDout[5]), .CIN(CIN), .B4(B4), .A4(A4), .B3(B3), .A3(A3), .B2(B2), .A2(A2), .B1(B1), .A1(A1),
    .B0(B0), .A0(A0), .C4(ADDout[4]), .C3(ADDout[3]), .C2(ADDout[2]), .C1(ADDout[1]), .C0(ADDout[0]));
  AND and_1 (
    .A0(A0), .B0(B0), .A1(A1), .B1(B1), .A2(A2), .B2(B2), .A3(A3), .B3(B3), .A4(A4), .B4(B4), .C0(ANDout[0]),
    .C1(ANDout[1]), .C2(ANDout[2]), .C3(ANDout[3]), .C4(ANDout[4]));
  OR or_1 (
    .A0(A0), .B0(B0), .A1(A1), .B1(B1), .A2(A2), .B2(B2), .A3(A3), .B3(B3), .A4(A4), .B4(B4), .C0(ORout[0]),
    .C1(ORout[1]), .C2(ORout[2]), .C3(ORout[3]), .C4(ORout[4]));
  NOT not_1 (
    .A0(A0), .A1(A1), .A2(A2), .A3(A3), .A4(A4), .C0(NOTout[0]), .C1(NOTout[1]), .C2(NOTout[2]),
    .C3(NOTout[3]), .C4(NOTout[4]));
  // Probe on {CIN, ANDout}
  // Probe on {CIN, ORout}
  SLL sll_1 (
    .CIN(CIN), .A0(A0), .A1(A1), .A2(A2), .A3(A3), .A4(A4), .C0(SLLout[0]), .C1(SLLout[1]), .C2(SLLout[2]),
    .C3(SLLout[3]), .C4(SLLout[4]), .Cout(SLLout[5]));
  // Probe on SLLout
  SRL srl_1 (
    .A0(A0), .A1(A1), .A2(A2), .A3(A3), .A4(A4), .C0(SLRout[0]), .C1(SLRout[1]), .C2(SLRout[2]),
    .C3(SLRout[3]), .C4(SLRout[4]), .Cin(SRLBit));
  // Probe on {1'b0, SLRout}
  Multiplexer #(.select(3), .width(6)) multiplexer_1 (
    .in0({CIN, ANDout}), .in1({CIN, ORout}), .in2({CIN, NOTout}), .in3(ADDout),
    .in4({CIN, A4, A3, A2, A1, A0}), .in5(SLLout), .in6({1'b0, SLRout}), .in7({CIN, B4, B3, B2, B1, B0}),
    .out({C5, C4, C3, C2, C1, C0}), .sel({S2, S1, S0}));  // open: en
  // Probe on {C5, C4, C3, C2, C1, C0}
  // Probe on {S2, S1, S0}

  // Other names for the same wires on the sheet: Carry = ADDout[5]; MOVIout[5:0] = {CIN, B4, B3, B2, B1, B0};
  //   MOVout[5:0] = {CIN, A4, A3, A2, A1, A0}; ANDout[5] = CIN; NOTout[5] = CIN; ORout[5] = CIN;
  //   Select[2:0] = {S2, S1, S0}
endmodule

module NOT (
  input  A0,
  input  A1,
  input  A2,
  input  A3,
  input  A4,
  output C0,
  output C1,
  output C2,
  output C3,
  output C4
);

  not not_1 (C0, A0);
  not not_2 (C1, A1);
  not not_3 (C2, A2);
  not not_4 (C3, A3);
  not not_5 (C4, A4);
endmodule

module AND (
  input  A0,
  input  B0,
  input  A1,
  input  B1,
  input  A2,
  input  B2,
  input  A3,
  input  B3,
  input  A4,
  input  B4,
  output C0,
  output C1,
  output C2,
  output C3,
  output C4
);

  and and_1 (C0, A0, B0);
  and and_2 (C1, A1, B1);
  and and_3 (C2, A2, B2);
  and and_4 (C3, A3, B3);
  and and_5 (C4, A4, B4);
endmodule

module OR (
  input  A0,
  input  B0,
  input  A1,
  input  B1,
  input  A2,
  input  B2,
  input  A3,
  input  B3,
  input  A4,
  input  B4,
  output C0,
  output C1,
  output C2,
  output C3,
  output C4
);

  or or_1 (C0, A0, B0);
  or or_2 (C1, A1, B1);
  or or_3 (C2, A2, B2);
  or or_4 (C3, A3, B3);
  or or_5 (C4, A4, B4);
endmodule

module CLA (
  input  C0,
  input  G0,
  input  P0,
  input  G1,
  input  P1,
  input  G2,
  input  P2,
  input  G3,
  input  P3,
  input  G4,
  input  P4,
  output C1,
  output C2,
  output C3,
  output C4,
  output C5
);

  wire P0C0_out, P1G0_out, P1P0C0_out, P2G1_out, P2P1G0_out, P2P1P0C0_out, P3G2_out, P3P2G1_out,
       P3P2P1G0_out, P3P2P1P0C0_out, P4G3_out, P4P3G2_out, P4P3P2G1_out, P4P3P2P1G0_out, P4P3P2P1P0C0_out;

  and P0C0 (P0C0_out, P0, C0);
  or u_C1 (C1, P0C0_out, G0);
  and P1G0 (P1G0_out, P1, G0);
  and P1P0C0 (P1P0C0_out, P1, P0, C0);
  or u_C2 (C2, P1G0_out, P1P0C0_out, G1);
  and P2G1 (P2G1_out, P2, G1);
  and P2P1G0 (P2P1G0_out, P2, P1, G0);
  or u_C3 (C3, P2G1_out, P2P1G0_out, P2P1P0C0_out, G2);
  and P2P1P0C0 (P2P1P0C0_out, P2, P1, P0, C0);
  and P3G2 (P3G2_out, P3, G2);
  and P3P2G1 (P3P2G1_out, P3, P2, G1);
  and P3P2P1G0 (P3P2P1G0_out, P3, P2, P1, G0);
  or u_C4 (C4, P3G2_out, P3P2G1_out, P3P2P1G0_out, P3P2P1P0C0_out, G3);
  and P3P2P1P0C0 (P3P2P1P0C0_out, P3, P2, P1, P0, C0);
  and P4G3 (P4G3_out, P4, G3);
  and P4P3G2 (P4P3G2_out, P4, P3, G2);
  and P4P3P2G1 (P4P3P2G1_out, P4, P3, P2, G1);
  or u_C5 (C5, P4G3_out, P4P3G2_out, P4P3P2G1_out, P4P3P2P1G0_out, P4P3P2P1P0C0_out, G4);
  and P4P3P2P1G0 (P4P3P2P1G0_out, P4, P3, P2, P1, G0);
  and P4P3P2P1P0C0 (P4P3P2P1P0C0_out, P4, P3, P2, P1, P0, C0);
endmodule

module FullAdder (
  input  A,
  input  B,
  input  CIn,
  output Sum,
  output COut,
  output G,
  output P
);

  wire and_1_out, and_2_out, xor_1_out;

  and u_G (G, A, B);
  or u_P (P, A, B);
  xor xor_1 (xor_1_out, A, B);
  and and_1 (and_1_out, A, B);
  and and_2 (and_2_out, xor_1_out, CIn);
  xor xor_2 (Sum, xor_1_out, CIn);
  or or_1 (COut, and_2_out, and_1_out);
endmodule

module ADD (
  input  B4,
  input  A4,
  input  B3,
  input  A3,
  input  B2,
  input  A2,
  input  B1,
  input  A1,
  input  B0,
  input  A0,
  input  CIN,
  output C5,
  output C4,
  output C3,
  output C2,
  output C1,
  output C0
);

  wire cla_1_c1, cla_1_c2, cla_1_c3, cla_1_c4, fulladder_1_g, fulladder_1_p, fulladder_2_g, fulladder_2_p,
       fulladder_3_g, fulladder_3_p, fulladder_4_g, fulladder_4_p, fulladder_5_g, fulladder_5_p;

  FullAdder fulladder_1 (.A(B3), .B(A3), .CIn(cla_1_c3), .Sum(C3), .G(fulladder_1_g), .P(fulladder_1_p));  // open: COut
  FullAdder fulladder_2 (.A(B4), .B(A4), .CIn(cla_1_c4), .Sum(C4), .G(fulladder_2_g), .P(fulladder_2_p));  // open: COut
  CLA cla_1 (
    .C0(CIN), .G0(fulladder_4_g), .P0(fulladder_4_p), .G1(fulladder_5_g), .P1(fulladder_5_p),
    .G2(fulladder_3_g), .P2(fulladder_3_p), .G3(fulladder_1_g), .P3(fulladder_1_p), .G4(fulladder_2_g),
    .P4(fulladder_2_p), .C1(cla_1_c1), .C2(cla_1_c2), .C3(cla_1_c3), .C4(cla_1_c4), .C5(C5));
  FullAdder fulladder_3 (.A(B2), .B(A2), .CIn(cla_1_c2), .Sum(C2), .G(fulladder_3_g), .P(fulladder_3_p));  // open: COut
  FullAdder fulladder_4 (.A(B0), .B(A0), .CIn(CIN), .Sum(C0), .G(fulladder_4_g), .P(fulladder_4_p));  // open: COut
  FullAdder fulladder_5 (.A(B1), .B(A1), .CIn(cla_1_c1), .Sum(C1), .G(fulladder_5_g), .P(fulladder_5_p));  // open: COut
endmodule

module SLL (
  input  CIN,
  input  A0,
  input  A1,
  input  A2,
  input  A3,
  input  A4,
  output C0,
  output C1,
  output C2,
  output C3,
  output C4,
  output Cout
);


  assign C0 = CIN;
  assign C1 = A0;
  assign C2 = A1;
  assign C3 = A2;
  assign C4 = A3;
  assign Cout = A4;
endmodule

module SRL (
  input  A0,
  input  A1,
  input  A2,
  input  A3,
  input  A4,
  input  Cin,
  output C0,
  output C1,
  output C2,
  output C3,
  output C4
);


  assign C0 = A1;
  assign C1 = A2;
  assign C2 = A3;
  assign C3 = A4;
  assign C4 = Cin;
endmodule

// PC Adder
module PCAdder (
  input  [4:0] IN,
  input  [4:0] _1_or_5,
  output COUT,
  output [4:0] OUT
);

  ADD add_1 (
    .C5(COUT), .CIN(1'b0), .B4(IN[4]), .A4(_1_or_5[4]), .B3(IN[3]), .A3(_1_or_5[3]), .B2(IN[2]),
    .A2(_1_or_5[2]), .B1(IN[1]), .A1(_1_or_5[1]), .B0(IN[0]), .A0(_1_or_5[0]), .C4(OUT[4]), .C3(OUT[3]),
    .C2(OUT[2]), .C1(OUT[1]), .C0(OUT[0]));
endmodule
